// Logisim project Single_Cycle_Processor.circ as structural Verilog: 2 circuits, main circuit Single_Cycle_Processor
module Single_Cycle_Processor (
  input  Jump_Signal,
  input  Brach_Signal
);

  wire ALUSrc, clock_1_out, Ext, MemRd, MemtoReg, MemWr, RegSource, RegWr;
  wire [4:0] ImmL, instruction_spliter_1_rd, instruction_spliter_1_rs1, instruction_spliter_1_rs2,
       multiplexer_2_out;
  wire [5:0] OpCode;
  wire [10:0] Function, ImmH, ImmU;
  wire [15:0] Imm16;
  wire [19:0] ALUControl, BranshPC, JumpPC, PC, pc_1_1_outpcplus1, Register_q;
  wire [31:0] ALUIn, ALUOut, B, data_memory_1_p6, Extended, instruction_memory_1__32_bit_iinstruction,
       Output, register_file_1_busa, Rs1;

  Clock clock_1 (.out(clock_1_out));
  Jump jump_1 (.Imm16(Imm16), .Rs1(Rs1), .Pc_jump(JumpPC), .initial_pc(PC));
  Multiplexer #(.select(2), .width(20), .enable("false")) multiplexer_1 (
    .in0({20{1'b0}}), .in1(BranshPC), .in2(JumpPC), .in3(pc_1_1_outpcplus1), .out(PC),
    .sel({Jump_Signal, Brach_Signal}));
  Register #(.width(20)) Register (.D(PC), .Q(Register_q), .clk(clock_1_out));  // open: en, clr
  PC_1 pc_1_1 (.Initial_Pc(Register_q), .OutPcPlus1(pc_1_1_outpcplus1));
  Branch_pc branch_pc_1 (.ImmL(ImmL), .ImmU(ImmH), .initial_pc(PC), .Pc_Branch(BranshPC));
  ALU_Control alu_control_1 (.Opcode(OpCode), .Function(Function), .ALU_Control(ALUControl));
  Instruction_Memory instruction_memory_1 (
    .PC(Register_q), ._32_bit_iinstruction(instruction_memory_1__32_bit_iinstruction));
  Instruction_Spliter instruction_spliter_1 (
    .in_1(instruction_memory_1__32_bit_iinstruction), .Opcode(OpCode), .RD(instruction_spliter_1_rd),
    .ImmL(ImmL), .Rs1(instruction_spliter_1_rs1), .Rs2(instruction_spliter_1_rs2), .ImmU(ImmU), .F(Function),
    .Imm16(Imm16));
  Multiplexer #(.width(5), .enable("false")) multiplexer_2 (
    .in0(instruction_spliter_1_rs1), .in1(instruction_spliter_1_rd), .out(multiplexer_2_out), .sel(RegSource));
  Storage_Control_Unit storage_control_unit_1 (
    .RegSrc(RegSource), .RegWr(RegWr), .MemRd(MemRd), .MemWr(MemWr), .MemtoReg(MemtoReg), .in_1(OpCode));
  Register_File register_file_1 (
    .BusW(Output), .RegWrite(RegWr), .BusA(register_file_1_busa), .BusB(B), .Rs1(multiplexer_2_out),
    .Rs2(instruction_spliter_1_rs2), .Clock(clock_1_out), .Rd(instruction_spliter_1_rd));  // open: R2, R3, R4, R5, R6, R7, R8, R9, R10, R11, R12, R14, R15, R16, R17, R18, R19, R20, R21, R22, R23, R24, R25, R26, R27, R28, R29, R30, R31, R1, R13
  Op_Control op_control_1 (.ExtOp(Ext), .ALUSrc(ALUSrc), ._6_bit_Op(OpCode));
  Extender extender_1 (.Immediate(Imm16), .Extender_Op(Ext), .Immediate_2(Extended));
  ALU alu_1 (
    .Rs(register_file_1_busa), .Rt(ALUIn), .ALU_Output(ALUOut), .ALU_Control(ALUControl));  // open: Overflow, Branch, Zero
  Multiplexer #(.width(32), .enable("false")) multiplexer_3 (.in0(Extended), .in1(B), .out(ALUIn), .sel(ALUSrc));
  // Data_Memory data_memory_1: pin names not known; wires that end beside it: ALUOut, B, clock_1_out, MemRd, MemWr, data_memory_1_p6
  Multiplexer #(.width(32), .enable("false")) multiplexer_4 (
    .in0(ALUOut), .in1(data_memory_1_p6), .out(Output), .sel(MemtoReg));
endmodule

module Instruction_Spliter (
  input  [31:0] in_1,
  output [5:0] Opcode,
  output [4:0] RD,
  output [4:0] ImmL,
  output [4:0] Rs1,
  output [15:0] Imm16,
  output [10:0] F,
  output [10:0] ImmU,
  output [4:0] Rs2
);

  Register #(.width(32)) register_1 (.D(in_1), .Q({F, Imm16[4:0], Rs1, ImmL, Opcode}));  // open: en, clk, clr

  assign Imm16[15:5] = F;
  assign ImmU = F;
  assign RD = ImmL;
  assign Rs2 = Imm16[4:0];

  // Notes on the sheet:
  //   SB_Type
  //   R_Tube
  //   I-Type
endmodule
